// Logisim project gate.circ as structural Verilog: 1 circuit, main circuit main
module main (
  input  in_1,
  input  in_2,
  input  in_3,
  input  in_4,
  input  in_5,
  input  in_6,
  input  in_7,
  output out_8,
  output out_9,
  output out_10
);

  wire nand_1_out, nand_2_out, nand_3_out, nand_4_out, nor_1_out, nor_2_out;

  nand nand_1 (nand_1_out, in_1, in_1);
  nand nand_2 (nand_2_out, in_2, in_3);
  nand nand_3 (nand_3_out, in_4, in_4);
  nand nand_4 (nand_4_out, in_5, in_5);
  nor nor_1 (nor_1_out, in_6, in_6);
  nor nor_2 (nor_2_out, in_7, in_7);
  nand nand_5 (out_8, nand_2_out, nand_2_out);
  nand nand_6 (out_9, nand_3_out, nand_4_out);
  nor nor_3 (out_10, nor_1_out, nor_2_out);
  LED led_1 (.in(nand_1_out));
endmodule
